// Logisim project cpu.circ as structural Verilog: 1 circuit, main circuit cpu
module cpu (
  input  Rest
);

  wire alu_1_zero, Clk_out, main_1_aluopr, main_1_alusrc, main_1_memtoreg, main_1_regdst, main_1_regwren;
  wire [3:0] main_1_memwrmask;
  wire [4:0] alucontroller_1_alu_out, multiplexer_1_out;
  wire [31:0] adder_1_out, alu_1_result, DataMem_memreaddata, multiplexer_2_out, PC_q, RegisterFile_p4,
       RegisterFile_p7, RegisterFile_p8, signextend_1_extended;

  Clock Clk (.out(Clk_out));
  Register #(.width(32)) PC (.D(adder_1_out), .en(1'b1), .clk(Clk_out), .Q(PC_q), .clr(Rest));
  Adder #(.width(32)) adder_1 (.a(32'h4), .b(PC_q), .out(adder_1_out));  // open: cin, cout
  mem InstMem (.MemAddress(PC_q), .clk(Clk_out));  // open: MemWriteMask, MemWriteData, MemReadData
  Multiplexer #(.width(5)) multiplexer_1 (
    .in0({5{1'b0}}), .in1(5'b00010), .out(multiplexer_1_out), .sel(main_1_regdst));
  Control_main main_1 (
    .Opcode({6{1'b0}}), .RegDst(main_1_regdst), .RegWrEn(main_1_regwren), .AluSrc(main_1_alusrc),
    .MemToReg(main_1_memtoreg), .AluOpr(main_1_aluopr), .MemWrMask(main_1_memwrmask));  // open: Branch, Jump
  // regfile RegisterFile: pin names not known; wires that end beside it: {5{1'b0}}, {5{1'b0}}, multiplexer_1_out, RegisterFile_p4, main_1_regwren, Clk_out, RegisterFile_p7, RegisterFile_p8
  signExtend signextend_1 (.Immd(16'h1200), .Extended(signextend_1_extended));
  Multiplexer #(.width(32)) multiplexer_2 (
    .in0(RegisterFile_p8), .in1(signextend_1_extended), .out(multiplexer_2_out), .sel(main_1_alusrc));
  AluController alucontroller_1 (
    .func({6{1'b0}}), .opcode({6{1'b0}}), .aluOperation(main_1_aluopr), .ALU_out(alucontroller_1_alu_out));
  ALU alu_1 (
    .ReadData1(RegisterFile_p7), .ReadData2(multiplexer_2_out), .ControlBits(alucontroller_1_alu_out),
    .Result(alu_1_result), .Zero(alu_1_zero));
  mem DataMem (
    .MemAddress(alu_1_result), .MemWriteMask(main_1_memwrmask), .MemWriteData(RegisterFile_p8),
    .clk(Clk_out), .MemReadData(DataMem_memreaddata));
  Multiplexer #(.width(32)) multiplexer_3 (
    .in0(alu_1_result), .in1(DataMem_memreaddata), .out(RegisterFile_p4), .sel(main_1_memtoreg));
endmodule
